# Fritzing sketch robocar (saved by Fritzing 0.9.3b)
breadboards: 1

parts:
  M1 = Dagu DGServo 9g (Pan and tilt) [part_number=RS001B]
  HC-SR04_Sensor_1 = HC-SR04 Ultrasonic Distance Sensor
  поиск_пути = LED - 5mm [color="Red (633nm)" package="5 mm [THT]"]
  Part1 = Arduino Uno (Rev3) - ICSP
  R1 = Resistor [tolerance=±5% resistance=220 package=THT]
  фара_1 = LEDs [package=led10mm]
  фара_2 = LEDs [package=led10mm]
  R2 = Resistor [tolerance=±5% resistance=220 package=THT]
  габарит2 = LED - 5mm [color="Red (633nm)" package="5 mm [THT]"]
  задний_ход = LEDs [package=led10mm]
  R3 = Resistor [tolerance=±5% resistance=220 package=THT]
  R4 = Resistor [tolerance=±5% resistance=220 package=THT]
  габарит1 = LED - 5mm [color="Red (633nm)" package="5 mm [THT]"]
  поворотник_лево = LED - 3mm [color="Red (633nm)" package="3 mm [THT]"]
  R5 = Resistor [tolerance=±5% resistance=220 package=THT]
  поворотник_право = LED - 3mm [color="Red (633nm)" package="3 mm [THT]"]
  R7 = Resistor [tolerance=±5% resistance=220 package=THT]
  S2 = H-Bridge with L298N
  VCC2 = Battery block 9V

nets:
  GND: M1.gnd, поиск_пути.cathode, поворотник_лево.cathode, поворотник_право.cathode, S2.GND, VCC2.-
  N1: M1.pulse, Part1.D10_PWM/SS
  N2: HC-SR04_Sensor_1.VCC, R2.Pin_1, габарит2.anode
  N3: HC-SR04_Sensor_1.TRIG, Part1.D8
  N4: HC-SR04_Sensor_1.ECHO, Part1.D9_PWM
  N5: HC-SR04_Sensor_1.GND, R3.Pin_0, R4.Pin_0
  N6: поиск_пути.anode, R1.Pin_0
  N7: Part1.A0, R1.Pin_1
  N8: Part1.A1, R5.Pin_1
  N9: Part1.A2, R7.Pin_1
  N10: Part1.D2, S2.IN1
  N11: Part1.D3_PWM, S2.IN2
  N12: Part1.D5_PWM, S2.IN3
  N13: Part1.D6_PWM, S2.IN4
  N14: Part1.D7, задний_ход.A
  N15: фара_1.A, фара_2.C
  N16: фара_2.A, R2.Pin_0
  N17: габарит2.cathode, габарит1.anode
  N18: задний_ход.C, R3.Pin_1
  N19: R4.Pin_1, габарит1.cathode
  N20: поворотник_лево.anode, R5.Pin_0
  N21: поворотник_право.anode, R7.Pin_0
  N22: S2.12V, VCC2.+

custom parts:
  H-Bridge with L298N: h-bridge
